# Fritzing sketch PCB (saved by Fritzing 0.9.3b)
breadboards: 1

parts:
  WeMos_D1_Mini1 = WeMos D1 Mini
  LED1 = RGB LED (com. cathode, rgb) [package="5 mm [THT]"]
  LED2 = RGB LED (com. cathode, rgb) [package="5 mm [THT]"]
  LED3 = RGB LED (com. cathode, rgb) [package="5 mm [THT]"]
  LED4 = RGB LED (com. cathode, rgb) [package="5 mm [THT]"]

nets:
  N1: WeMos_D1_Mini1.D1, LED1.blue_anode, LED2.blue_anode, LED3.blue_anode, LED4.blue_anode
  N2: WeMos_D1_Mini1.D2, LED1.green_anode, LED2.green_anode, LED3.green_anode, LED4.green_anode
  N3: WeMos_D1_Mini1.D3, LED1.red_anode, LED2.red_anode, LED3.red_anode, LED4.red_anode
  N4: LED1.common_cathode, LED2.common_cathode, LED3.common_cathode, LED4.common_cathode

custom parts:
  WeMos D1 Mini: The D1 mini is a mini wifi board based on ESP-8266EX.
